// Logisim project cpu (2).circ as structural Verilog: 30 circuits, main circuit HalfAdder
module HalfAdder (
  input  A,
  input  B,
  output Carry,
  output Sum
);

  and and_1 (Carry, A, B);
  xor xor_1 (Sum, A, B);
endmodule

module FullAdder (
  input  A,
  input  B,
  input  C_in,
  output C_out,
  output R
);

  wire halfadder_1_carry, halfadder_1_sum, halfadder_2_carry;

  HalfAdder halfadder_1 (.A(A), .B(B), .Carry(halfadder_1_carry), .Sum(halfadder_1_sum));
  HalfAdder halfadder_2 (.A(halfadder_1_sum), .B(C_in), .Carry(halfadder_2_carry), .Sum(R));
  or or_1 (C_out, halfadder_1_carry, halfadder_2_carry);
endmodule

module Adder8Bit (
  input  [7:0] B,
  input  [7:0] A,
  input  Operation,
  output [7:0] Output
);

  wire fulladder_1_c_out, fulladder_2_c_out, fulladder_3_c_out, fulladder_4_c_out, fulladder_5_c_out,
       fulladder_6_c_out, fulladder_7_c_out, fulladder_8_c_out, xor_1_out, xor_2_out, xor_3_out, xor_4_out,
       xor_5_out, xor_6_out, xor_7_out, xor_8_out;

  xor xor_1 (xor_1_out, Operation, B[0]);
  xor xor_2 (xor_2_out, B[1], Operation);
  xor xor_3 (xor_3_out, B[2], Operation);
  xor xor_4 (xor_4_out, B[3], Operation);
  xor xor_5 (xor_5_out, B[4], Operation);
  xor xor_6 (xor_6_out, B[5], Operation);
  xor xor_7 (xor_7_out, B[6], Operation);
  xor xor_8 (xor_8_out, B[7], Operation);
  FullAdder fulladder_1 (.A(A[0]), .B(xor_1_out), .C_in(Operation), .C_out(fulladder_1_c_out), .R(Output[0]));
  FullAdder fulladder_2 (.A(A[1]), .B(xor_2_out), .C_in(fulladder_1_c_out), .C_out(fulladder_2_c_out), .R(Output[1]));
  FullAdder fulladder_3 (.A(A[2]), .B(xor_3_out), .C_in(fulladder_2_c_out), .C_out(fulladder_3_c_out), .R(Output[2]));
  FullAdder fulladder_4 (.A(A[3]), .B(xor_4_out), .C_in(fulladder_3_c_out), .C_out(fulladder_4_c_out), .R(Output[3]));
  FullAdder fulladder_5 (.A(A[4]), .B(xor_5_out), .C_in(fulladder_4_c_out), .C_out(fulladder_5_c_out), .R(Output[4]));
  FullAdder fulladder_6 (.A(A[5]), .B(xor_6_out), .C_in(fulladder_5_c_out), .C_out(fulladder_6_c_out), .R(Output[5]));
  FullAdder fulladder_7 (.A(A[6]), .B(xor_7_out), .C_in(fulladder_6_c_out), .C_out(fulladder_7_c_out), .R(Output[6]));
  FullAdder fulladder_8 (.A(A[7]), .B(xor_8_out), .C_in(fulladder_7_c_out), .C_out(fulladder_8_c_out), .R(Output[7]));
  // also tied to GND on the sheet: fulladder_8_c_out
endmodule

module _1BitMemory (
  input  Input,
  input  Set,
  output Output
);

  wire nand_1_out, nand_2_out, nand_4_out;

  nand nand_1 (nand_1_out, Input, Set);
  nand nand_2 (nand_2_out, nand_1_out, Set);
  nand nand_3 (Output, nand_1_out, nand_4_out);
  nand nand_4 (nand_4_out, Output, nand_2_out);

  // Notes on the sheet:
  //   Input: pull=down
endmodule

module _8BitRegister (
  input  Set,
  input  Enable,
  input  [7:0] Input,
  output [7:0] Output
);

  wire [7:0] n1bitmemory_1_output, n8bitenable_1_output;

  _1BitMemory u_1bitmemory_1 (.Input(Input[0]), .Set(Set), .Output(n1bitmemory_1_output[0]));
  _1BitMemory u_1bitmemory_2 (.Input(Input[1]), .Set(Set), .Output(n1bitmemory_1_output[1]));
  _1BitMemory u_1bitmemory_3 (.Input(Input[2]), .Set(Set), .Output(n1bitmemory_1_output[2]));
  _1BitMemory u_1bitmemory_4 (.Input(Input[3]), .Set(Set), .Output(n1bitmemory_1_output[3]));
  _1BitMemory u_1bitmemory_5 (.Input(Input[4]), .Set(Set), .Output(n1bitmemory_1_output[4]));
  _1BitMemory u_1bitmemory_6 (.Input(Input[5]), .Set(Set), .Output(n1bitmemory_1_output[5]));
  _1BitMemory u_1bitmemory_7 (.Input(Input[6]), .Set(Set), .Output(n1bitmemory_1_output[6]));
  _1BitMemory u_1bitmemory_8 (.Input(Input[7]), .Set(Set), .Output(n1bitmemory_1_output[7]));
  _8BitEnable u_8bitenable_1 (.Input(n1bitmemory_1_output), .Output(n8bitenable_1_output), .Enable(Enable));
  assign Output = Enable ? n8bitenable_1_output : 8'bz;  // Controlled_Buffer controlled_buffer_1

  // Notes on the sheet:
  //   Input: pull=down
endmodule

module _16BitRegister (
  input  Enable,
  input  Set,
  input  [15:0] Input,
  output [15:0] Output
);

  wire [15:0] n1bitmemory_1_output, n16bitenable_1_output;

  _1BitMemory u_1bitmemory_1 (.Input(Input[0]), .Set(Set), .Output(n1bitmemory_1_output[0]));
  _1BitMemory u_1bitmemory_2 (.Input(Input[1]), .Set(Set), .Output(n1bitmemory_1_output[1]));
  _1BitMemory u_1bitmemory_3 (.Input(Input[2]), .Set(Set), .Output(n1bitmemory_1_output[2]));
  _1BitMemory u_1bitmemory_4 (.Input(Input[3]), .Set(Set), .Output(n1bitmemory_1_output[3]));
  _1BitMemory u_1bitmemory_5 (.Input(Input[4]), .Set(Set), .Output(n1bitmemory_1_output[4]));
  _1BitMemory u_1bitmemory_6 (.Input(Input[5]), .Set(Set), .Output(n1bitmemory_1_output[5]));
  _1BitMemory u_1bitmemory_7 (.Input(Input[6]), .Set(Set), .Output(n1bitmemory_1_output[6]));
  _1BitMemory u_1bitmemory_8 (.Input(Input[7]), .Set(Set), .Output(n1bitmemory_1_output[7]));
  _1BitMemory u_1bitmemory_9 (.Input(Input[8]), .Set(Set), .Output(n1bitmemory_1_output[8]));
  _1BitMemory u_1bitmemory_10 (.Input(Input[9]), .Set(Set), .Output(n1bitmemory_1_output[9]));
  _1BitMemory u_1bitmemory_11 (.Input(Input[10]), .Set(Set), .Output(n1bitmemory_1_output[10]));
  _1BitMemory u_1bitmemory_12 (.Input(Input[11]), .Set(Set), .Output(n1bitmemory_1_output[11]));
  _1BitMemory u_1bitmemory_13 (.Input(Input[12]), .Set(Set), .Output(n1bitmemory_1_output[12]));
  _1BitMemory u_1bitmemory_14 (.Input(Input[13]), .Set(Set), .Output(n1bitmemory_1_output[13]));
  _1BitMemory u_1bitmemory_15 (.Input(Input[14]), .Set(Set), .Output(n1bitmemory_1_output[14]));
  _1BitMemory u_1bitmemory_16 (.Input(Input[15]), .Set(Set), .Output(n1bitmemory_1_output[15]));
  _16BitEnable u_16bitenable_1 (.Input(n1bitmemory_1_output), .Output(n16bitenable_1_output), .Enable(Enable));
  assign Output = Enable ? n16bitenable_1_output : 16'bz;  // Controlled_Buffer controlled_buffer_1

  // Notes on the sheet:
  //   Input: pull=down
endmodule

module Adder16Bit (
  input  [15:0] A,
  input  [15:0] B,
  input  Operation,
  output [15:0] Output
);

  wire fulladder_1_c_out, fulladder_2_c_out, fulladder_3_c_out, fulladder_4_c_out, fulladder_5_c_out,
       fulladder_6_c_out, fulladder_7_c_out, fulladder_8_c_out, fulladder_9_c_out, fulladder_10_c_out,
       fulladder_11_c_out, fulladder_12_c_out, fulladder_13_c_out, fulladder_14_c_out, fulladder_15_c_out,
       fulladder_16_c_out, xor_1_out, xor_2_out, xor_3_out, xor_4_out, xor_5_out, xor_6_out, xor_7_out,
       xor_8_out, xor_9_out, xor_10_out, xor_11_out, xor_12_out, xor_13_out, xor_14_out, xor_15_out,
       xor_16_out;

  xor xor_1 (xor_1_out, B[0], Operation);
  xor xor_2 (xor_2_out, B[1], Operation);
  xor xor_3 (xor_3_out, B[2], Operation);
  xor xor_4 (xor_4_out, B[3], Operation);
  xor xor_5 (xor_5_out, B[4], Operation);
  xor xor_6 (xor_6_out, B[5], Operation);
  xor xor_7 (xor_7_out, B[6], Operation);
  xor xor_8 (xor_8_out, B[7], Operation);
  xor xor_9 (xor_9_out, B[8], Operation);
  xor xor_10 (xor_10_out, B[9], Operation);
  xor xor_11 (xor_11_out, B[10], Operation);
  xor xor_12 (xor_12_out, B[11], Operation);
  xor xor_13 (xor_13_out, B[12], Operation);
  xor xor_14 (xor_14_out, B[13], Operation);
  xor xor_15 (xor_15_out, B[14], Operation);
  xor xor_16 (xor_16_out, B[15], Operation);
  FullAdder fulladder_1 (.A(A[0]), .B(xor_1_out), .C_in(Operation), .C_out(fulladder_1_c_out), .R(Output[0]));
  FullAdder fulladder_2 (.A(A[1]), .B(xor_2_out), .C_in(fulladder_1_c_out), .C_out(fulladder_2_c_out), .R(Output[1]));
  FullAdder fulladder_3 (.A(A[2]), .B(xor_3_out), .C_in(fulladder_2_c_out), .C_out(fulladder_3_c_out), .R(Output[2]));
  FullAdder fulladder_4 (.A(A[3]), .B(xor_4_out), .C_in(fulladder_3_c_out), .C_out(fulladder_4_c_out), .R(Output[3]));
  FullAdder fulladder_5 (.A(A[4]), .B(xor_5_out), .C_in(fulladder_4_c_out), .C_out(fulladder_5_c_out), .R(Output[4]));
  FullAdder fulladder_6 (.A(A[5]), .B(xor_6_out), .C_in(fulladder_5_c_out), .C_out(fulladder_6_c_out), .R(Output[5]));
  FullAdder fulladder_7 (.A(A[6]), .B(xor_7_out), .C_in(fulladder_6_c_out), .C_out(fulladder_7_c_out), .R(Output[6]));
  FullAdder fulladder_8 (.A(A[7]), .B(xor_8_out), .C_in(fulladder_7_c_out), .C_out(fulladder_8_c_out), .R(Output[7]));
  FullAdder fulladder_9 (.A(A[8]), .B(xor_9_out), .C_in(fulladder_8_c_out), .C_out(fulladder_9_c_out), .R(Output[8]));
  FullAdder fulladder_10 (
    .A(A[9]), .B(xor_10_out), .C_in(fulladder_9_c_out), .C_out(fulladder_10_c_out), .R(Output[9]));
  FullAdder fulladder_11 (
    .A(A[10]), .B(xor_11_out), .C_in(fulladder_10_c_out), .C_out(fulladder_11_c_out), .R(Output[10]));
  FullAdder fulladder_12 (
    .A(A[11]), .B(xor_12_out), .C_in(fulladder_11_c_out), .C_out(fulladder_12_c_out), .R(Output[11]));
  FullAdder fulladder_13 (
    .A(A[12]), .B(xor_13_out), .C_in(fulladder_12_c_out), .C_out(fulladder_13_c_out), .R(Output[12]));
  FullAdder fulladder_14 (
    .A(A[13]), .B(xor_14_out), .C_in(fulladder_13_c_out), .C_out(fulladder_14_c_out), .R(Output[13]));
  FullAdder fulladder_15 (
    .A(A[14]), .B(xor_15_out), .C_in(fulladder_14_c_out), .C_out(fulladder_15_c_out), .R(Output[14]));
  FullAdder fulladder_16 (
    .A(A[15]), .B(xor_16_out), .C_in(fulladder_15_c_out), .C_out(fulladder_16_c_out), .R(Output[15]));
  // also tied to GND on the sheet: fulladder_16_c_out
endmodule

module _3x8Decoder (
  input  [2:0] Input,
  output out_2,
  output out_3,
  output out_4,
  output out_5,
  output out_6,
  output out_7,
  output out_8,
  output out_9
);

  wire not_1_out, not_2_out, not_3_out;

  not not_1 (not_1_out, Input[2]);
  not not_2 (not_2_out, Input[1]);
  not not_3 (not_3_out, Input[0]);
  and and_1 (out_2, not_3_out, not_2_out, not_1_out);
  and and_2 (out_3, Input[0], not_2_out, not_1_out);
  and and_3 (out_4, not_3_out, Input[1], not_1_out);
  and and_4 (out_5, Input[0], Input[1], not_1_out);
  and and_5 (out_6, not_3_out, not_2_out, Input[2]);
  and and_6 (out_7, Input[0], not_2_out, Input[2]);
  and and_7 (out_8, not_3_out, Input[1], Input[2]);
  and and_8 (out_9, Input[0], Input[1], Input[2]);
endmodule

module _8x16bitRAM (
  input  Set,
  input  Reset,
  input  [15:0] in_3,
  input  Enable,
  input  [7:0] in_5,
  output [15:0] out_6
);

  wire and_1_out, and_2_out, and_3_out, and_4_out, and_5_out, and_6_out, and_7_out, and_8_out, and_9_out,
       and_10_out, and_11_out, and_12_out, and_13_out, and_14_out, and_15_out, and_16_out,
       n3x8decoder_1_out_2, n3x8decoder_1_out_3, n3x8decoder_1_out_4, n3x8decoder_1_out_5,
       n3x8decoder_1_out_6, n3x8decoder_1_out_7, n3x8decoder_1_out_8, n3x8decoder_1_out_9, or_1_out,
       or_2_out, or_3_out, or_4_out, or_5_out, or_6_out, or_7_out, or_8_out;

  _3x8Decoder u_3x8decoder_1 (
    .Input(in_5[2:0]), .out_2(n3x8decoder_1_out_2), .out_3(n3x8decoder_1_out_3), .out_4(n3x8decoder_1_out_4),
    .out_5(n3x8decoder_1_out_5), .out_6(n3x8decoder_1_out_6), .out_7(n3x8decoder_1_out_7),
    .out_8(n3x8decoder_1_out_8), .out_9(n3x8decoder_1_out_9));
  and and_1 (and_1_out, n3x8decoder_1_out_2, Set);
  and and_2 (and_2_out, n3x8decoder_1_out_3, Set);
  and and_3 (and_3_out, n3x8decoder_1_out_4, Set);
  and and_4 (and_4_out, n3x8decoder_1_out_5, Set);
  and and_5 (and_5_out, n3x8decoder_1_out_6, Set);
  and and_6 (and_6_out, n3x8decoder_1_out_7, Set);
  and and_7 (and_7_out, n3x8decoder_1_out_8, Set);
  and and_8 (and_8_out, n3x8decoder_1_out_9, Set);
  or or_1 (or_1_out, Reset, and_1_out);
  or or_2 (or_2_out, Reset, and_2_out);
  or or_3 (or_3_out, Reset, and_3_out);
  or or_4 (or_4_out, Reset, and_4_out);
  or or_5 (or_5_out, Reset, and_5_out);
  or or_6 (or_6_out, Reset, and_6_out);
  or or_7 (or_7_out, Reset, and_7_out);
  or or_8 (or_8_out, Reset, and_8_out);
  _16BitRegister u_16bitregister_1 (.Input(in_3), .Output(out_6), .Set(or_1_out), .Enable(and_9_out));
  _16BitRegister u_16bitregister_2 (.Input(in_3), .Output(out_6), .Set(or_2_out), .Enable(and_10_out));
  _16BitRegister u_16bitregister_3 (.Input(in_3), .Output(out_6), .Set(or_3_out), .Enable(and_11_out));
  _16BitRegister u_16bitregister_4 (.Input(in_3), .Output(out_6), .Set(or_4_out), .Enable(and_12_out));
  _16BitRegister u_16bitregister_5 (.Input(in_3), .Output(out_6), .Set(or_5_out), .Enable(and_13_out));
  _16BitRegister u_16bitregister_6 (.Input(in_3), .Output(out_6), .Set(or_6_out), .Enable(and_14_out));
  _16BitRegister u_16bitregister_7 (.Input(in_3), .Output(out_6), .Set(or_7_out), .Enable(and_15_out));
  _16BitRegister u_16bitregister_8 (.Input(in_3), .Output(out_6), .Set(or_8_out), .Enable(and_16_out));
  and and_9 (and_9_out, Enable, n3x8decoder_1_out_2);
  and and_10 (and_10_out, Enable, n3x8decoder_1_out_3);
  and and_11 (and_11_out, Enable, n3x8decoder_1_out_4);
  and and_12 (and_12_out, Enable, n3x8decoder_1_out_5);
  and and_13 (and_13_out, Enable, n3x8decoder_1_out_6);
  and and_14 (and_14_out, Enable, n3x8decoder_1_out_7);
  and and_15 (and_15_out, Enable, n3x8decoder_1_out_8);
  and and_16 (and_16_out, Enable, n3x8decoder_1_out_9);
endmodule

module CPU (
  input  in_1,
  output [7:0] out_2,
  output [15:0] out_3,
  output [15:0] out_4
);

  wire ACC_E, ACC_S, ADDER_E, BUS_1, CLK_out, IR_S, MAR_E, MAR_S, N, N_S, OP, or_1_out, or_2_out, PC_E, PC_S,
       PS_E, PS_SH, PS_SL, RAM_E, RAM_S, REG0_E, REG0_S, REG1_E, REG1_S, REG2_E, REG2_S, REG3_E, REG3_S,
       SHL_E, SHR_E, stepper_1_out_4, stepper_1_out_5, stepper_1_out_6, stepper_1_out_7, stepper_1_out_8,
       stepper_1_out_9, stepper_1_out_10, stepper_1_set, Stop, Temp_E, Temp_S, Z, Z_S, zero_1_out_2;
  wire [15:0] adder16bit_1_output, bus1_1_out_3, leftshifter_1_output, n16bitenable_2_output,
       programstorage_1_out_4, rightshifter_1_output, Temp_output;

  Clock CLK (.out(CLK_out));
  or or_1 (or_1_out, CLK_out, Stop);
  ProgramStorage programstorage_1 (
    .in_3(out_3[7:0]), .out_4(programstorage_1_out_4), .Set_lower(PS_SL), .Set_higher(PS_SH));
  _16BitRegister u_16bitregister_1 (.Input(out_3), .Output(out_3), .Set(REG0_S), .Enable(REG0_E));
  _16BitEnable u_16bitenable_1 (.Input(programstorage_1_out_4), .Output(out_3), .Enable(PS_E));
  _16BitRegister u_16bitregister_2 (.Input(out_3), .Output(out_3), .Set(REG1_S), .Enable(REG1_E));
  _16BitRegister u_16bitregister_3 (.Input(out_3), .Output(out_3), .Set(REG2_S), .Enable(REG2_E));
  Stepper stepper_1 (
    .out_6(stepper_1_out_6), .out_7(stepper_1_out_7), .out_10(stepper_1_out_10), .out_4(stepper_1_out_4),
    .out_5(stepper_1_out_5), .Clock(or_1_out), .Reset(in_1), .out_8(stepper_1_out_8),
    .out_9(stepper_1_out_9), .Set(stepper_1_set));
  _8BitRegister u_8bitregister_1 (.Input(programstorage_1_out_4[7:0]), .Output(out_2), .Set(IR_S), .Enable(1'b1));
  or or_2 (or_2_out, in_1, stepper_1_set);
  _16BitRegister u_16bitregister_4 (.Input(out_3), .Output(out_3), .Set(REG3_S), .Enable(REG3_E));
  ControlSection controlsection_1 (
    .Bus1(BUS_1), .ACC_E(ACC_E), .ACC_S(ACC_S), .PC_E(PC_E), .PC_S(PC_S), .PS_SL(PS_SL), .PS_SH(PS_SH),
    .PS_E(PS_E), .IR_S(IR_S), .Instruction(out_2), .REG0_S(REG0_S), .REG1_S(REG1_S), .REG2_S(REG2_S),
    .REG3_S(REG3_S), .Step_0(stepper_1_out_6), .Step_1(stepper_1_out_7), .Step_2(stepper_1_out_8),
    .Step_3(stepper_1_out_9), .Step_4(stepper_1_out_10), .Step_5(stepper_1_out_4), .Step_6(stepper_1_out_5),
    .Reset(in_1), .Temp_S(Temp_S), .REG0_E(REG0_E), .REG1_E(REG1_E), .REG2_E(REG2_E), .REG3_E(REG3_E),
    .Temp_E(Temp_E), .OP(OP), .MAR_E(MAR_E), .MAR_S(MAR_S), .RAM_S(RAM_S), .RAM_E(RAM_E), .in_6(or_2_out),
    .ADDER_E(ADDER_E), .SHL_E(SHL_E), .Stop(Stop), .SHR_E(SHR_E), .N_S(N_S), .in_7(N), .in_8(Z), .Z_S(Z_S));
  _16BitRegister Temp (.Input(out_3), .Output(Temp_output), .Set(Temp_S), .Enable(Temp_E));
  LED led_1 (.in(Stop));
  _16BitRegister MAR (.Input(out_3), .Output(out_4), .Set(MAR_S), .Enable(MAR_E));
  _1BitMemory u_1bitmemory_1 (.Input(out_3[15]), .Set(N_S), .Output(N));
  Bus1 bus1_1 (.in_1(BUS_1), .in_2(Temp_output), .out_3(bus1_1_out_3));
  Zero zero_1 (.in_1(out_3), .out_2(zero_1_out_2));
  _8x16bitRAM u_8x16bitram_1 (
    .in_5(out_4[7:0]), .in_3(out_3), .Enable(RAM_E), .out_6(out_3), .Set(RAM_S), .Reset(in_1));
  _1BitMemory u_1bitmemory_2 (.Input(zero_1_out_2), .Set(Z_S), .Output(Z));
  Adder16Bit adder16bit_1 (.A(bus1_1_out_3), .B(out_3), .Output(adder16bit_1_output), .Operation(OP));
  LeftShifter leftshifter_1 (.Input(out_3), .Output(leftshifter_1_output));
  RightShifter rightshifter_1 (.Input(out_3), .Output(rightshifter_1_output));
  _16BitEnable u_16bitenable_2 (.Input(adder16bit_1_output), .Output(n16bitenable_2_output), .Enable(ADDER_E));
  _16BitEnable u_16bitenable_3 (.Input(leftshifter_1_output), .Output(n16bitenable_2_output), .Enable(SHL_E));
  _16BitEnable u_16bitenable_4 (.Input(rightshifter_1_output), .Output(n16bitenable_2_output), .Enable(SHR_E));
  _16BitRegister Accumulator (.Input(n16bitenable_2_output), .Output(out_3), .Set(ACC_S), .Enable(ACC_E));
  _16BitRegister u_16bitregister_5 (.Input(out_3), .Output(out_3), .Set(PC_S), .Enable(PC_E));

  // Other names for the same wires on the sheet: RESET = in_1

  // Notes on the sheet:
  //   Instruction Register
  //   Program Counter
endmodule

module _16BitEnable (
  input  Enable,
  input  [15:0] Input,
  output [15:0] Output
);

  wire and_1_out, and_2_out, and_3_out, and_4_out, and_5_out, and_6_out, and_7_out, and_8_out, and_9_out,
       and_10_out, and_11_out, and_12_out, and_13_out, and_14_out, and_15_out, and_16_out;

  and and_1 (and_1_out, Input[0], Enable);
  assign Output[0] = Enable ? and_1_out : 1'bz;  // Controlled_Buffer controlled_buffer_1
  and and_2 (and_2_out, Input[1], Enable);
  assign Output[1] = Enable ? and_2_out : 1'bz;  // Controlled_Buffer controlled_buffer_2
  and and_3 (and_3_out, Input[2], Enable);
  assign Output[2] = Enable ? and_3_out : 1'bz;  // Controlled_Buffer controlled_buffer_3
  assign Output[3] = Enable ? and_4_out : 1'bz;  // Controlled_Buffer controlled_buffer_4
  and and_4 (and_4_out, Input[3], Enable);
  and and_5 (and_5_out, Input[4], Enable);
  assign Output[4] = Enable ? and_5_out : 1'bz;  // Controlled_Buffer controlled_buffer_5
  and and_6 (and_6_out, Input[5], Enable);
  assign Output[5] = Enable ? and_6_out : 1'bz;  // Controlled_Buffer controlled_buffer_6
  and and_7 (and_7_out, Input[6], Enable);
  assign Output[6] = Enable ? and_7_out : 1'bz;  // Controlled_Buffer controlled_buffer_7
  and and_8 (and_8_out, Input[7], Enable);
  assign Output[7] = Enable ? and_8_out : 1'bz;  // Controlled_Buffer controlled_buffer_8
  and and_9 (and_9_out, Input[8], Enable);
  assign Output[8] = Enable ? and_9_out : 1'bz;  // Controlled_Buffer controlled_buffer_9
  and and_10 (and_10_out, Input[9], Enable);
  assign Output[9] = Enable ? and_10_out : 1'bz;  // Controlled_Buffer controlled_buffer_10
  and and_11 (and_11_out, Input[10], Enable);
  assign Output[10] = Enable ? and_11_out : 1'bz;  // Controlled_Buffer controlled_buffer_11
  assign Output[11] = Enable ? and_12_out : 1'bz;  // Controlled_Buffer controlled_buffer_12
  and and_12 (and_12_out, Input[11], Enable);
  and and_13 (and_13_out, Input[12], Enable);
  assign Output[12] = Enable ? and_13_out : 1'bz;  // Controlled_Buffer controlled_buffer_13
  assign Output[13] = Enable ? and_14_out : 1'bz;  // Controlled_Buffer controlled_buffer_14
  and and_14 (and_14_out, Input[13], Enable);
  and and_15 (and_15_out, Input[14], Enable);
  assign Output[14] = Enable ? and_15_out : 1'bz;  // Controlled_Buffer controlled_buffer_15
  and and_16 (and_16_out, Input[15], Enable);
  assign Output[15] = Enable ? and_16_out : 1'bz;  // Controlled_Buffer controlled_buffer_16

  // Notes on the sheet:
  //   Output: pull=down
endmodule

module _2x4Decoder (
  input  [1:0] Input,
  output out_2,
  output out_3,
  output out_4,
  output out_5
);

  wire not_1_out, not_2_out;

  not not_1 (not_1_out, Input[1]);
  not not_2 (not_2_out, Input[0]);
  and and_1 (out_2, not_2_out, not_1_out);
  and and_2 (out_3, Input[0], not_1_out);
  and and_3 (out_4, not_2_out, Input[1]);
  and and_4 (out_5, Input[0], Input[1]);
endmodule

module ProgramStorage (
  input  Set_higher,
  input  Set_lower,
  input  [7:0] in_3,
  output [15:0] out_4
);

  wire [7:0] rom_1_data;

  ROM rom_1 (.addr(in_3), .data(rom_1_data));  // open: sel
  _8BitRegister Lower (.Input(rom_1_data), .Output(out_4[7:0]), .Set(Set_lower), .Enable(1'b1));
  _8BitRegister Higher (.Input(rom_1_data), .Output(out_4[15:8]), .Set(Set_higher), .Enable(1'b1));

  // Notes on the sheet:
  //   in_3: pull=down
  //   contents of rom_1 (hex, n*v repeats v):
  //   93 0 8 63 c4 0 37 cc 0 37 92 0 1 1e 62 cc 0 37 93 0 1 1b 63 cc 0 34 90 0 0 91 0 1 4 92 0 1 1e 62 c4
  //   0 37 1f b 1a 2 10 4 15 9 c0 0 20 90 0 1 98
endmodule

module _8BitEnable (
  input  Enable,
  input  [7:0] Input,
  output [7:0] Output
);

  wire and_1_out, and_2_out, and_3_out, and_4_out, and_5_out, and_6_out, and_7_out, and_8_out;

  and and_1 (and_1_out, Input[0], Enable);
  assign Output[0] = Enable ? and_1_out : 1'bz;  // Controlled_Buffer controlled_buffer_1
  and and_2 (and_2_out, Input[1], Enable);
  assign Output[1] = Enable ? and_2_out : 1'bz;  // Controlled_Buffer controlled_buffer_2
  assign Output[2] = Enable ? and_3_out : 1'bz;  // Controlled_Buffer controlled_buffer_3
  and and_3 (and_3_out, Input[2], Enable);
  and and_4 (and_4_out, Input[3], Enable);
  assign Output[3] = Enable ? and_4_out : 1'bz;  // Controlled_Buffer controlled_buffer_4
  and and_5 (and_5_out, Input[4], Enable);
  assign Output[4] = Enable ? and_5_out : 1'bz;  // Controlled_Buffer controlled_buffer_5
  and and_6 (and_6_out, Input[5], Enable);
  assign Output[5] = Enable ? and_6_out : 1'bz;  // Controlled_Buffer controlled_buffer_6
  and and_7 (and_7_out, Input[6], Enable);
  assign Output[6] = Enable ? and_7_out : 1'bz;  // Controlled_Buffer controlled_buffer_7
  and and_8 (and_8_out, Input[7], Enable);
  assign Output[7] = Enable ? and_8_out : 1'bz;  // Controlled_Buffer controlled_buffer_8
endmodule

module Bus1 (
  input  in_1,
  input  [15:0] in_2,
  output [15:0] out_3
);

  wire not_1_out;

  not not_1 (not_1_out, in_1);
  or or_1 (out_3[0], in_2[0], in_1);
  and and_1 (out_3[1], in_2[1], not_1_out);
  and and_2 (out_3[2], in_2[2], not_1_out);
  and and_3 (out_3[3], in_2[3], not_1_out);
  and and_4 (out_3[4], in_2[4], not_1_out);
  and and_5 (out_3[5], in_2[5], not_1_out);
  and and_6 (out_3[6], in_2[6], not_1_out);
  and and_7 (out_3[7], in_2[7], not_1_out);
  and and_8 (out_3[8], in_2[8], not_1_out);
  and and_9 (out_3[9], in_2[9], not_1_out);
  and and_10 (out_3[10], in_2[10], not_1_out);
  and and_11 (out_3[11], in_2[11], not_1_out);
  and and_12 (out_3[12], in_2[12], not_1_out);
  and and_13 (out_3[13], in_2[13], not_1_out);
  and and_14 (out_3[14], in_2[14], not_1_out);
  and and_15 (out_3[15], in_2[15], not_1_out);
endmodule

module ControlSection (
  input  Step_2,
  input  Step_3,
  input  Step_4,
  input  Step_5,
  input  Step_6,
  input  in_6,
  input  in_7,
  input  in_8,
  input  Step_0,
  input  Step_1,
  input  Reset,
  input  [7:0] Instruction,
  output MAR_S,
  output RAM_S,
  output MAR_E,
  output RAM_E,
  output ADDER_E,
  output Temp_E,
  output REG0_E,
  output Temp_S,
  output REG1_E,
  output SHL_E,
  output REG2_E,
  output SHR_E,
  output Bus1,
  output REG3_E,
  output ACC_E,
  output OP,
  output Stop,
  output ACC_S,
  output Z_S,
  output N_S,
  output PC_E,
  output PC_S,
  output REG0_S,
  output PS_SL,
  output REG1_S,
  output PS_SH,
  output REG2_S,
  output PS_E,
  output REG3_S,
  output IR_S
);

  wire addandsub_1_acc_e, addandsub_1_acc_s, addandsub_1_adder_e, addandsub_1_reg_e_first,
       addandsub_1_reg_e_second, addandsub_1_reg_s, addandsub_1_temp_s, and_8_out, and_9_out, and_10_out,
       and_11_out, and_12_out, and_13_out, and_14_out, and_15_out, and_16_out, and_17_out, and_18_out,
       and_19_out, and_20_out, and_21_out, and_22_out, inc_1_acc_e, inc_1_acc_s, inc_1_adder_e, inc_1_bus1,
       inc_1_reg_e_second, inc_1_reg_s, instructiondecoder_1_add, instructiondecoder_1_inc,
       instructiondecoder_1_jump, instructiondecoder_1_load, instructiondecoder_1_read,
       instructiondecoder_1_stop, instructiondecoder_1_store, instructiondecoder_1_sub,
       instructiondecoder_1_test, JMPR, JN, jumpreg_1_pc_s, jumpreg_1_reg_e_second, JZ,
       loadjump_jn_jz_1_acc_e, loadjump_jn_jz_1_acc_s, loadjump_jn_jz_1_adder_e, loadjump_jn_jz_1_bus1,
       loadjump_jn_jz_1_pc_e, loadjump_jn_jz_1_pc_s, loadjump_jn_jz_1_ps_sh, loadjump_jn_jz_1_ps_sl,
       loadjump_jn_jz_1_reg_s, n2x4decoder_1_out_2, n2x4decoder_1_out_3, n2x4decoder_1_out_4,
       n2x4decoder_1_out_5, n2x4decoder_2_out_2, n2x4decoder_2_out_3, n2x4decoder_2_out_4,
       n2x4decoder_2_out_5, N_S_t, or_4_out, or_6_out, or_7_out, or_8_out, or_9_out, or_10_out, or_11_out,
       or_12_out, or_13_out, shiftleft_1_acc_e, shiftleft_1_acc_s, shiftleft_1_reg_e_second,
       shiftleft_1_reg_s, shiftright_1_acc_e, shiftright_1_acc_s, shiftright_1_reg_e_second,
       shiftright_1_reg_s, SHL, SHR, storeandread_1_mar_s, storeandread_1_ram_s, storeandread_1_reg_e_first,
       storeandread_1_reg_e_second, storeandread_1_reg_s, test_1_z_s, Z_S_t;

  and and_1 (ACC_S, in_6, or_4_out);
  and and_2 (PC_S, in_6, or_6_out);
  and and_3 (PS_SL, in_6, or_7_out);
  and and_4 (PS_SH, in_6, or_8_out);
  and and_5 (IR_S, in_6, Step_0);
  and and_6 (MAR_S, in_6, storeandread_1_mar_s);
  or or_1 (ADDER_E, Step_0, addandsub_1_adder_e, inc_1_adder_e, loadjump_jn_jz_1_adder_e);
  and and_7 (Temp_S, in_6, addandsub_1_temp_s);
  or or_2 (Bus1, inc_1_bus1, loadjump_jn_jz_1_bus1, Step_0);
  or or_3 (ACC_E, inc_1_acc_e, addandsub_1_acc_e, or_10_out, loadjump_jn_jz_1_acc_e, Step_1);
  or or_4 (or_4_out, inc_1_acc_s, addandsub_1_acc_s, or_9_out, loadjump_jn_jz_1_acc_s, Step_0);
  or or_5 (PC_E, loadjump_jn_jz_1_pc_e, Step_0);
  or or_6 (or_6_out, loadjump_jn_jz_1_pc_s, jumpreg_1_pc_s, Step_1, Reset);
  or or_7 (or_7_out, loadjump_jn_jz_1_ps_sl, Reset, Step_0);
  or or_8 (or_8_out, Reset, loadjump_jn_jz_1_ps_sh);
  AddAndSub addandsub_1 (
    .Temp_S(addandsub_1_temp_s), .REG_E_FIRST(addandsub_1_reg_e_first), .Temp_E(Temp_E),
    .REG_E_SECOND(addandsub_1_reg_e_second), .ACC_S(addandsub_1_acc_s), .ACC_E(addandsub_1_acc_e),
    .REG_S(addandsub_1_reg_s), .OP(OP), .Step_2(Step_2), .Step_3(Step_3), .Step_4(Step_4),
    .Add(instructiondecoder_1_add), .Sub(instructiondecoder_1_sub), .ADDER_E(addandsub_1_adder_e));
  Inc inc_1 (
    .REG_E_SECOND(inc_1_reg_e_second), .Bus1(inc_1_bus1), .ACC_S(inc_1_acc_s), .ACC_E(inc_1_acc_e),
    .REG_S(inc_1_reg_s), .Step_2(Step_2), .Step_3(Step_3), .Inc(instructiondecoder_1_inc),
    .ADDER_E(inc_1_adder_e));
  LoadJump_JN_JZ loadjump_jn_jz_1 (
    .Bus1(loadjump_jn_jz_1_bus1), .PS_SH(loadjump_jn_jz_1_ps_sh), .PS_SL(loadjump_jn_jz_1_ps_sl),
    .ACC_E(loadjump_jn_jz_1_acc_e), .ACC_S(loadjump_jn_jz_1_acc_s), .PC_E(loadjump_jn_jz_1_pc_e),
    .PC_S(loadjump_jn_jz_1_pc_s), .PS_E(PS_E), .REG_S(loadjump_jn_jz_1_reg_s), .Step_1(Step_1),
    .Step_2(Step_2), .Step_3(Step_3), .Step_4(Step_4), .Step_5(Step_5), .Step_6(Step_6),
    .Load(instructiondecoder_1_load), .Jump(instructiondecoder_1_jump), .ADDER_E(loadjump_jn_jz_1_adder_e),
    .JN(JN), .N(in_7), .JZ(JZ), .Z(in_8));
  StoreAndRead storeandread_1 (
    .MAR_S(storeandread_1_mar_s), .REG_E_FIRST(storeandread_1_reg_e_first), .MAR_E(MAR_E),
    .REG_E_SECOND(storeandread_1_reg_e_second), .RAM_S(storeandread_1_ram_s), .RAM_E(RAM_E),
    .REG_S(storeandread_1_reg_s), .Step_2(Step_2), .Step_3(Step_3), .Store(instructiondecoder_1_store),
    .Read(instructiondecoder_1_read));
  JumpReg jumpreg_1 (.PC_S(jumpreg_1_pc_s), .REG_E_SECOND(jumpreg_1_reg_e_second), .JMPR(JMPR), .Step2(Step_2));
  or or_9 (or_9_out, shiftright_1_acc_s, shiftleft_1_acc_s);
  or or_10 (or_10_out, shiftright_1_acc_e, shiftleft_1_acc_e);
  Stop stop_1 (.Stop_2(Stop), .STOP(instructiondecoder_1_stop), .Step_2(Step_2));
  InstructionDecoder instructiondecoder_1 (
    .in_1(Instruction[7:2]), .LOAD(instructiondecoder_1_load), .ADD(instructiondecoder_1_add),
    .SUB(instructiondecoder_1_sub), .JUMP(instructiondecoder_1_jump), .STORE(instructiondecoder_1_store),
    .READ(instructiondecoder_1_read), .INC(instructiondecoder_1_inc), .SHL(SHL), .SHR(SHR), .JMPR(JMPR),
    .STOP(instructiondecoder_1_stop), .JN(JN), .TEST(instructiondecoder_1_test), .JZ(JZ));
  ShiftLeft shiftleft_1 (
    .REG_E_SECOND(shiftleft_1_reg_e_second), .ACC_S(shiftleft_1_acc_s), .SHL_E(SHL_E),
    .ACC_E(shiftleft_1_acc_e), .REG_S(shiftleft_1_reg_s), .Step_2(Step_2), .Step_3(Step_3), .Shl(SHL));
  ShiftRight shiftright_1 (
    .REG_E_SECOND(shiftright_1_reg_e_second), .ACC_S(shiftright_1_acc_s), .SHR_E(SHR_E),
    .ACC_E(shiftright_1_acc_e), .REG_S(shiftright_1_reg_s), .Step_2(Step_2), .Step_3(Step_3), .Shr(SHR));
  Test test_1 (.N_S(N_S_t), .Step_2(Step_2), .TEST(instructiondecoder_1_test), .REG_E_SECOND(Z_S_t), .Z_S(test_1_z_s));
  or or_11 (or_11_out, addandsub_1_reg_e_first, storeandread_1_reg_e_first);
  or or_12 (or_12_out, shiftleft_1_reg_s, shiftright_1_reg_s, inc_1_reg_s, addandsub_1_reg_s, storeandread_1_reg_s, loadjump_jn_jz_1_reg_s);
  or or_13 (or_13_out, shiftleft_1_reg_e_second, storeandread_1_reg_e_second, inc_1_reg_e_second, jumpreg_1_reg_e_second, addandsub_1_reg_e_second, shiftright_1_reg_e_second, test_1_z_s);
  and and_8 (and_8_out, in_6, or_12_out);
  _2x4Decoder u_2x4decoder_1 (
    .Input(Instruction[3:2]), .out_2(n2x4decoder_1_out_2), .out_3(n2x4decoder_1_out_3),
    .out_4(n2x4decoder_1_out_4), .out_5(n2x4decoder_1_out_5));
  and and_9 (and_9_out, or_11_out, n2x4decoder_1_out_2);
  and and_10 (and_10_out, or_11_out, n2x4decoder_1_out_3);
  and and_11 (and_11_out, or_11_out, n2x4decoder_1_out_4);
  and and_12 (and_12_out, or_11_out, n2x4decoder_1_out_5);
  _2x4Decoder u_2x4decoder_2 (
    .Input(Instruction[1:0]), .out_2(n2x4decoder_2_out_2), .out_3(n2x4decoder_2_out_3),
    .out_4(n2x4decoder_2_out_4), .out_5(n2x4decoder_2_out_5));
  and and_13 (and_13_out, or_13_out, n2x4decoder_2_out_2);
  and and_14 (and_14_out, or_13_out, n2x4decoder_2_out_3);
  and and_15 (and_15_out, or_13_out, n2x4decoder_2_out_4);
  and and_16 (and_16_out, or_13_out, n2x4decoder_2_out_5);
  and and_17 (and_17_out, and_8_out, n2x4decoder_2_out_2);
  and and_18 (and_18_out, and_8_out, n2x4decoder_2_out_3);
  and and_19 (and_19_out, and_8_out, n2x4decoder_2_out_4);
  and and_20 (and_20_out, and_8_out, n2x4decoder_2_out_5);
  or or_14 (REG0_E, and_9_out, and_13_out);
  or or_15 (REG1_E, and_10_out, and_14_out);
  or or_16 (REG2_E, and_11_out, and_15_out);
  or or_17 (REG3_E, and_12_out, and_16_out);
  and and_21 (and_21_out, in_6, Z_S_t);
  and and_22 (and_22_out, in_6, N_S_t);
  and and_23 (RAM_S, in_6, storeandread_1_ram_s);
  or or_18 (Z_S, and_21_out, Reset);
  or or_19 (N_S, and_22_out, Reset);
  or or_20 (REG0_S, and_17_out, Reset);
  or or_21 (REG1_S, and_18_out, Reset);
  or or_22 (REG2_S, and_19_out, Reset);
  or or_23 (REG3_S, and_20_out, Reset);

  // Other names for the same wires on the sheet: N = in_7; Set = in_6; Z = in_8
endmodule

module InstructionDecoder (
  input  [5:0] in_1,
  output LOAD,
  output ADD,
  output SUB,
  output JUMP,
  output STORE,
  output READ,
  output INC,
  output SHL,
  output SHR,
  output JMPR,
  output STOP,
  output JN,
  output TEST,
  output JZ
);

  wire not_1_out, not_2_out, not_3_out, not_4_out, not_5_out, not_6_out;

  not not_1 (not_1_out, in_1[5]);
  not not_2 (not_2_out, in_1[4]);
  not not_3 (not_3_out, in_1[3]);
  not not_4 (not_4_out, in_1[2]);
  not not_5 (not_5_out, in_1[1]);
  not not_6 (not_6_out, in_1[0]);
  and and_1 (LOAD, in_1[5], not_2_out, not_3_out, in_1[2], not_5_out);
  and and_2 (ADD, not_1_out, not_2_out, not_3_out, not_4_out);
  and and_3 (SUB, not_1_out, not_2_out, not_3_out, in_1[2]);
  and and_4 (JUMP, in_1[5], in_1[4], not_3_out, not_4_out, not_5_out, not_6_out);
  and and_5 (STORE, in_1[5], not_2_out, in_1[3], not_4_out);
  and and_6 (READ, in_1[5], not_2_out, in_1[3], in_1[2]);
  and and_7 (INC, not_1_out, not_2_out, in_1[3], not_4_out);
  and and_8 (SHL, not_1_out, in_1[4], not_3_out, not_4_out);
  and and_9 (SHR, not_1_out, in_1[4], not_3_out, in_1[2]);
  and and_10 (JMPR, in_1[5], in_1[4], not_3_out, not_4_out, in_1[1], not_6_out);
  and and_11 (STOP, in_1[5], not_2_out, not_3_out, in_1[2], in_1[1]);
  and and_12 (JN, in_1[5], in_1[4], not_3_out, not_4_out, not_5_out, in_1[0]);
  and and_13 (TEST, not_1_out, in_1[4], in_1[3], not_4_out);
  and and_14 (JZ, in_1[5], in_1[4], not_3_out, not_4_out, in_1[1], in_1[0]);
endmodule

module Stepper (
  input  Reset,
  input  Clock,
  output Set,
  output out_4,
  output out_5,
  output out_6,
  output out_7,
  output out_8,
  output out_9,
  output out_10
);

  wire and_2_out, and_4_out, and_6_out, and_8_out, and_10_out, and_12_out, and_14_out, n1bitmemory_1_output,
       n1bitmemory_2_output, n1bitmemory_3_output, n1bitmemory_4_output, n1bitmemory_5_output,
       n1bitmemory_6_output, n1bitmemory_7_output, n1bitmemory_8_output, n1bitmemory_9_output,
       n1bitmemory_10_output, n1bitmemory_11_output, n1bitmemory_12_output, n1bitmemory_13_output,
       n1bitmemory_14_output, n1bitmemory_15_output, n1bitmemory_16_output, n1bitmemory_17_output,
       n1bitmemory_18_output, n1bitmemory_19_output, n1bitmemory_20_output, n1bitmemory_21_output,
       n1bitmemory_22_output, n1bitmemory_23_output, not_1_out, not_2_out, not_3_out, not_4_out, not_5_out,
       not_6_out, not_7_out, not_8_out, not_9_out, not_10_out, not_11_out, not_12_out, not_13_out,
       not_14_out, not_15_out, not_16_out, or_1_out, or_2_out, or_3_out;

  or or_1 (or_1_out, n1bitmemory_23_output, Reset);
  not not_1 (not_1_out, Clock);
  not not_2 (not_2_out, or_1_out);
  or or_2 (or_2_out, or_1_out, Clock);
  or or_3 (or_3_out, or_1_out, not_1_out);
  and and_1 (out_6, n1bitmemory_1_output, not_4_out);
  _1BitMemory u_1bitmemory_1 (.Input(not_2_out), .Set(or_2_out), .Output(n1bitmemory_1_output));
  and and_2 (and_2_out, n1bitmemory_2_output, not_3_out);
  _1BitMemory u_1bitmemory_2 (.Input(n1bitmemory_1_output), .Set(or_3_out), .Output(n1bitmemory_2_output));
  not not_3 (not_3_out, n1bitmemory_3_output);
  _1BitMemory u_1bitmemory_3 (.Input(n1bitmemory_2_output), .Set(or_2_out), .Output(n1bitmemory_3_output));
  and and_3 (out_7, n1bitmemory_4_output, not_6_out);
  not not_4 (not_4_out, n1bitmemory_4_output);
  _1BitMemory u_1bitmemory_4 (.Input(n1bitmemory_3_output), .Set(or_3_out), .Output(n1bitmemory_4_output));
  and and_4 (and_4_out, n1bitmemory_5_output, not_5_out);
  _1BitMemory u_1bitmemory_5 (.Input(n1bitmemory_4_output), .Set(or_2_out), .Output(n1bitmemory_5_output));
  not not_5 (not_5_out, n1bitmemory_6_output);
  _1BitMemory u_1bitmemory_6 (.Input(n1bitmemory_5_output), .Set(or_3_out), .Output(n1bitmemory_6_output));
  and and_5 (out_8, n1bitmemory_7_output, not_8_out);
  not not_6 (not_6_out, n1bitmemory_7_output);
  _1BitMemory u_1bitmemory_7 (.Input(n1bitmemory_6_output), .Set(or_2_out), .Output(n1bitmemory_7_output));
  and and_6 (and_6_out, n1bitmemory_8_output, not_7_out);
  _1BitMemory u_1bitmemory_8 (.Input(n1bitmemory_7_output), .Set(or_3_out), .Output(n1bitmemory_8_output));
  not not_7 (not_7_out, n1bitmemory_9_output);
  _1BitMemory u_1bitmemory_9 (.Input(n1bitmemory_8_output), .Set(or_2_out), .Output(n1bitmemory_9_output));
  and and_7 (out_9, n1bitmemory_10_output, not_10_out);
  not not_8 (not_8_out, n1bitmemory_10_output);
  _1BitMemory u_1bitmemory_10 (.Input(n1bitmemory_9_output), .Set(or_3_out), .Output(n1bitmemory_10_output));
  and and_8 (and_8_out, n1bitmemory_11_output, not_9_out);
  _1BitMemory u_1bitmemory_11 (.Input(n1bitmemory_10_output), .Set(or_2_out), .Output(n1bitmemory_11_output));
  or or_4 (Set, and_2_out, and_4_out, and_6_out, and_8_out, and_10_out, and_12_out, and_14_out);
  not not_9 (not_9_out, n1bitmemory_12_output);
  _1BitMemory u_1bitmemory_12 (.Input(n1bitmemory_11_output), .Set(or_3_out), .Output(n1bitmemory_12_output));
  and and_9 (out_10, n1bitmemory_13_output, not_12_out);
  not not_10 (not_10_out, n1bitmemory_13_output);
  _1BitMemory u_1bitmemory_13 (.Input(n1bitmemory_12_output), .Set(or_2_out), .Output(n1bitmemory_13_output));
  and and_10 (and_10_out, n1bitmemory_14_output, not_11_out);
  _1BitMemory u_1bitmemory_14 (.Input(n1bitmemory_13_output), .Set(or_3_out), .Output(n1bitmemory_14_output));
  not not_11 (not_11_out, n1bitmemory_15_output);
  _1BitMemory u_1bitmemory_15 (.Input(n1bitmemory_14_output), .Set(or_2_out), .Output(n1bitmemory_15_output));
  and and_11 (out_4, n1bitmemory_16_output, not_14_out);
  not not_12 (not_12_out, n1bitmemory_16_output);
  _1BitMemory u_1bitmemory_16 (.Input(n1bitmemory_15_output), .Set(or_3_out), .Output(n1bitmemory_16_output));
  and and_12 (and_12_out, n1bitmemory_17_output, not_13_out);
  _1BitMemory u_1bitmemory_17 (.Input(n1bitmemory_16_output), .Set(or_2_out), .Output(n1bitmemory_17_output));
  not not_13 (not_13_out, n1bitmemory_18_output);
  _1BitMemory u_1bitmemory_18 (.Input(n1bitmemory_17_output), .Set(or_3_out), .Output(n1bitmemory_18_output));
  and and_13 (out_5, n1bitmemory_19_output, not_16_out);
  not not_14 (not_14_out, n1bitmemory_19_output);
  _1BitMemory u_1bitmemory_19 (.Input(n1bitmemory_18_output), .Set(or_2_out), .Output(n1bitmemory_19_output));
  and and_14 (and_14_out, n1bitmemory_20_output, not_15_out);
  _1BitMemory u_1bitmemory_20 (.Input(n1bitmemory_19_output), .Set(or_3_out), .Output(n1bitmemory_20_output));
  not not_15 (not_15_out, n1bitmemory_21_output);
  _1BitMemory u_1bitmemory_21 (.Input(n1bitmemory_20_output), .Set(or_2_out), .Output(n1bitmemory_21_output));
  not not_16 (not_16_out, n1bitmemory_22_output);
  _1BitMemory u_1bitmemory_22 (.Input(n1bitmemory_21_output), .Set(or_3_out), .Output(n1bitmemory_22_output));
  _1BitMemory u_1bitmemory_23 (.Input(n1bitmemory_22_output), .Set(or_2_out), .Output(n1bitmemory_23_output));
endmodule

module LoadJump_JN_JZ (
  input  Step_1,
  input  Step_2,
  input  Step_3,
  input  Step_4,
  input  Step_5,
  input  Step_6,
  input  Load,
  input  Jump,
  input  JN,
  input  N,
  input  JZ,
  input  Z,
  output Bus1,
  output PS_SH,
  output PS_SL,
  output ACC_E,
  output ACC_S,
  output ADDER_E,
  output PC_E,
  output REG_S,
  output PC_S,
  output PS_E
);

  wire and_2_out, and_4_out, and_5_out, and_6_out, and_7_out, and_9_out, or_4_out, or_5_out, or_6_out;

  and and_1 (PS_SH, Step_1, or_6_out);
  or or_1 (PC_S, ACC_E, and_4_out);
  and and_2 (and_2_out, Step_2, or_6_out);
  or or_2 (ACC_S, and_2_out, and_5_out);
  or or_3 (ACC_E, PS_SL, and_6_out);
  and and_3 (PS_SL, Step_3, or_6_out);
  and and_4 (and_4_out, or_5_out, PS_E);
  and and_5 (and_5_out, Step_4, or_6_out);
  or or_4 (or_4_out, and_9_out, and_7_out);
  or or_5 (or_5_out, or_4_out, Jump);
  or or_6 (or_6_out, Load, Jump, JN, JZ);
  and and_6 (and_6_out, Step_5, or_6_out);
  and and_7 (and_7_out, JN, N);
  and and_8 (PS_E, Step_6, or_6_out);
  and and_9 (and_9_out, JZ, Z);
  and and_10 (REG_S, Step_6, Load);

  assign ADDER_E = ACC_S;
  assign Bus1 = ACC_S;
  assign PC_E = ACC_S;
endmodule

module AddAndSub (
  input  Step_2,
  input  Step_3,
  input  Step_4,
  input  Add,
  input  Sub,
  output Temp_S,
  output REG_E_FIRST,
  output Temp_E,
  output ACC_E,
  output REG_E_SECOND,
  output REG_S,
  output ACC_S,
  output ADDER_E,
  output OP
);

  wire or_1_out;

  and and_1 (REG_E_FIRST, Step_2, or_1_out);
  and and_2 (ACC_S, Step_3, or_1_out);
  or or_1 (or_1_out, Add, Sub);
  and and_3 (ACC_E, Step_4, or_1_out);
  and and_4 (OP, Step_3, Sub);

  assign ADDER_E = ACC_S;
  assign REG_E_SECOND = ACC_S;
  assign REG_S = ACC_E;
  assign Temp_E = ACC_S;
  assign Temp_S = REG_E_FIRST;
endmodule

module Inc (
  input  Step_2,
  input  Step_3,
  input  Inc,
  output REG_E_SECOND,
  output ACC_E,
  output Bus1,
  output REG_S,
  output ACC_S,
  output ADDER_E
);

  and and_1 (ACC_S, Step_2, Inc);
  and and_2 (ACC_E, Step_3, Inc);

  assign ADDER_E = ACC_S;
  assign Bus1 = ACC_S;
  assign REG_E_SECOND = ACC_S;
  assign REG_S = ACC_E;
endmodule

module StoreAndRead (
  input  Step_2,
  input  Step_3,
  input  Store,
  input  Read,
  output MAR_S,
  output REG_E_SECOND,
  output REG_E_FIRST,
  output RAM_S,
  output MAR_E,
  output RAM_E,
  output REG_S
);

  wire or_1_out;

  and and_1 (MAR_S, Step_2, or_1_out);
  and and_2 (MAR_E, Step_3, or_1_out);
  and and_3 (RAM_S, Step_3, Store);
  or or_1 (or_1_out, Store, Read);
  and and_4 (RAM_E, Step_3, Read);

  assign REG_E_FIRST = MAR_S;
  assign REG_E_SECOND = RAM_S;
  assign REG_S = RAM_E;
endmodule

module LeftShifter (
  input  [15:0] Input,
  output [15:0] Output
);


  assign Output = {Input[14:0], 1'b0};
  // also tied to GND on the sheet: Input[15]
endmodule

module ShiftLeft (
  input  Step_2,
  input  Step_3,
  input  Shl,
  output REG_E_SECOND,
  output ACC_E,
  output ACC_S,
  output REG_S,
  output SHL_E
);

  and and_1 (ACC_S, Step_2, Shl);
  and and_2 (ACC_E, Step_3, Shl);

  assign REG_E_SECOND = ACC_S;
  assign REG_S = ACC_E;
  assign SHL_E = ACC_S;
endmodule

module RightShifter (
  input  [15:0] Input,
  output [15:0] Output
);


  assign Output = {1'b0, Input[15:1]};
  // also tied to GND on the sheet: Input[0]
endmodule

module ShiftRight (
  input  Step_2,
  input  Step_3,
  input  Shr,
  output REG_E_SECOND,
  output ACC_E,
  output ACC_S,
  output REG_S,
  output SHR_E
);

  and and_1 (ACC_S, Step_2, Shr);
  and and_2 (ACC_E, Step_3, Shr);

  assign REG_E_SECOND = ACC_S;
  assign REG_S = ACC_E;
  assign SHR_E = ACC_S;
endmodule

module JumpReg (
  input  JMPR,
  input  Step2,
  output PC_S,
  output REG_E_SECOND
);

  and and_1 (PC_S, JMPR, Step2);

  assign REG_E_SECOND = PC_S;
endmodule

module Stop (
  input  STOP,
  input  Step_2,
  output Stop_2
);

  and and_1 (Stop_2, STOP, Step_2);
endmodule

module Test (
  input  Step_2,
  input  TEST,
  output N_S,
  output Z_S,
  output REG_E_SECOND
);

  and and_1 (N_S, Step_2, TEST);

  assign REG_E_SECOND = N_S;
  assign Z_S = N_S;
endmodule

module Zero (
  input  [15:0] in_1,
  output out_2
);

  wire or_1_out;

  or or_1 (or_1_out, in_1[0], in_1[1], in_1[2], in_1[3], in_1[4], in_1[5], in_1[6], in_1[7], in_1[8], in_1[9], in_1[10], in_1[11], in_1[12], in_1[13], in_1[14], in_1[15]);
  not not_1 (out_2, or_1_out);
endmodule
